# Fritzing sketch Schematic (saved by Fritzing 0.9.3b)
breadboards: 1

parts:
  R4 = Resistor [tolerance=±5% resistance=330 package=THT]
  R3 = Resistor [tolerance=±5% resistance=330 package=THT]
  R5 = Resistor [tolerance=±5% resistance=470 package=THT]
  R2 = Resistor [tolerance=±1% resistance=1k package=THT]
  R1 = Resistor [tolerance=±1% resistance=10k package=THT]
  Q1 = NPN-Transistor [package="TO92 [THT]"]
  J1 = Piezo Speaker
  LED1 = LED - 3mm [color="Green (555nm)" package="3 mm [THT]"]
  Q2 = PHOTOTRANSISTOR REFLECTIVE OBJECT SENSOR [package=qrb1114-side]

nets:
  GND: R4.Pin_0, Q1.E, Q2.A, Q2.E
  N1: R4.Pin_1, LED1.cathode
  AIN2: R3.Pin_0, Q2.C
  VS: R3.Pin_1, R2.Pin_0, R1.Pin_0, J1.pin1
  N2: R5.Pin_0, Q1.B
  FIO6: R5.Pin_1
  N3: R2.Pin_1, Q1.C, J1.pin2
  N4: R1.Pin_1, Q2.K
  FIO4: LED1.anode

notes:
  K
  A
  C
  E
